# Fritzing sketch Weather-PCB (saved by Fritzing 0.9.3b)
breadboards: 1

parts:
  U1 = NodeMCU V1.0
  R1 = Resistor [tolerance=±5% resistance=1k package=THT]
  R2 = Resistor [tolerance=±5% resistance=470 package=THT]
  LCD1 = LCD screen

nets:
  N1: U1.D2, LCD1.RS
  N2: U1.D3, LCD1.E
  3V3: U1.3V3, R2.Pin_0, R2.Pin_1, LCD1.VDD, LCD1.LED+
  GND: U1.GND, R1.Pin_0, R1.Pin_1, LCD1.VSS, LCD1.V0, LCD1.R/W, LCD1.LED-
  N3: U1.D5, LCD1.DB4
  N4: U1.D6, LCD1.DB5
  N5: U1.D7, LCD1.DB6
  N6: U1.D8, LCD1.DB7

custom parts:
  NodeMCU V1.0: ESP8266 based NodeMCU
